// Logisim project computador_simulado.circ as structural Verilog: 9 circuits, main circuit main
module main (
);

  wire ADD, CARREGAR_JUMP, CL0CK, CLEAR, clock_1_out, controlled_buffer_2_out, DMX_CONTROL, ENABLE_RA, EQ,
       GEQ, GT, HLT, JMP, LEQ, LT, MOV, MOVA, MUL, nand_1_out, nand_2_out, nand_3_out, nor_1_out, nor_2_out,
       not_1_out, not_2_out, not_3_out, or_1_out, RDM, RESET_RAM, STR, SUB, VERIFICAR_RA_1;
  wire [1:0] RX, RY;
  wire [3:0] INSTRUCAO;
  wire [4:0] ENDERECO_CONTADOR, ENDERECO_GERAL;
  wire [7:0] PALAVRA_RAM, PALAVRA_REGISTRADA, RA, ram_1_dout, RAM_DADOS, SR0, SR1, SR2, SR3, SRX, SRY, ULA,
       VALOR_REGISTRADOR;

  and and_1 (CARREGAR_JUMP, VERIFICAR_RA_1, JMP);
  ContadorDePrograma contadordeprograma_1 (
    .CLEAR(CLEAR), .STR(STR), .RDM(RDM), .SRY(SRY), .CL0CK(CL0CK), .CARREGAR_JUMP(CARREGAR_JUMP),
    .ENDERECO_CONTADOR(ENDERECO_CONTADOR));
  nand nand_1 (nand_1_out, 1'b1, RDM);
  nand nand_2 (nand_2_out, 1'b1, MOV);
  nand nand_3 (nand_3_out, 1'b1, MOVA);
  Clock clock_1 (.out(clock_1_out));
  assign CL0CK = not_1_out ? clock_1_out : 1'bz;  // Controlled_Buffer controlled_buffer_1
  not not_1 (not_1_out, HLT);
  RegistradorDeInstrucao registradordeinstrucao_1 (
    .CL0CK(CL0CK), .PALAVRA_MEMORIA(PALAVRA_RAM), .CLEAR(CLEAR), .PALAVRA_REGISTRADA(PALAVRA_REGISTRADA));
  RegistradorAcumulador registradoracumulador_1 (
    .ENABLE_RA(ENABLE_RA), .CL0CK(CL0CK), .ULA(ULA), .CLEAR(CLEAR), .RA(RA));
  BancoDeRegistradores bancoderegistradores_1 (
    .VALOR_REGISTRADOR(VALOR_REGISTRADOR), .CLEAR(CLEAR), .CL0CK(CL0CK), .RX(RX), .DMX(DMX_CONTROL),
    .SR3(SR3), .SR0(SR0), .SR1(SR1), .SR2(SR2));
  nand nand_4 (DMX_CONTROL, nand_1_out, nand_2_out, nand_3_out);
  Button button_1 (.out(CLEAR));
  Button button_2 (.out(RESET_RAM));
  UnidadeDeControle unidadedecontrole_1 (
    .PALAVRA_REGISTRADA(PALAVRA_REGISTRADA), .SR0(SR0), .SR1(SR1), .SR2(SR2), .SR3(SR3), .RA(RA),
    .RAM_DADOS(RAM_DADOS), .RX(RX), .ENABLE_RA(ENABLE_RA), .INSTRUCAO(INSTRUCAO), .EQ(EQ), .LT(LT), .GT(GT),
    .LEQ(LEQ), .GEQ(GEQ), .JMP(JMP), .MUL(MUL), .RY(RY), .ADD(ADD), .SUB(SUB), .MOV(MOV), .MOVA(MOVA),
    .SRY(SRY), .SRX(SRX), .RDM(RDM), .STR(STR), .VALOR_REGISTRADOR(VALOR_REGISTRADOR), .HLT(HLT));
  UnidadeLogicaAritmetica unidadelogicaaritmetica_1 (
    .EQ(EQ), .LT(LT), .GT(GT), .LEQ(LEQ), .GEQ(GEQ), .JMP(JMP), .MUL(MUL), .ADD(ADD), .SUB(SUB), .SRX(SRX),
    .SRY(SRY), .RA(RA), .ULA(ULA), .VERIFICAR_IGUALDADE_RA(VERIFICAR_RA_1));
  or or_1 (or_1_out, not_2_out, not_3_out);
  not not_2 (not_2_out, CARREGAR_JUMP);
  assign controlled_buffer_2_out = or_1_out ? STR : 1'bz;  // Controlled_Buffer controlled_buffer_2
  not not_3 (not_3_out, STR);
  RAM #(.addrWidth(5), .asyncread("true"), .clearpin("true")) ram_1 (
    .addr(ENDERECO_GERAL), .we(controlled_buffer_2_out), .clk(CL0CK), .din(SRY), .dout(ram_1_dout),
    .clr(RESET_RAM));  // open: oe
  assign ENDERECO_GERAL = RDM ? {3'b111, RY} : 5'bz;  // Controlled_Buffer controlled_buffer_3
  assign ENDERECO_GERAL = STR ? {3'b111, RX} : 5'bz;  // Controlled_Buffer controlled_buffer_4
  assign ENDERECO_GERAL = nor_1_out ? ENDERECO_CONTADOR : 5'bz;  // Controlled_Buffer controlled_buffer_5
  nor nor_1 (nor_1_out, RDM, STR);
  assign RAM_DADOS = RDM ? ram_1_dout : 8'bz;  // Controlled_Buffer controlled_buffer_6
  assign PALAVRA_RAM = nor_2_out ? ram_1_dout : 8'bz;  // Controlled_Buffer controlled_buffer_7
  nor nor_2 (nor_2_out, RDM, STR);

  // Notes on the sheet:
  //   CONTROLE
  //   UNIDADE CENTRAL DE PROCESSAMENTO
  //   ARQUITETURA MATA38-2024
  //   PIPELINE DE EXECUCAO: BUSCAR-DECODIFICAR-EXECUTAR
  //   MEMORIA DE ACESSO ALEATORIA
endmodule

module ContadorDePrograma (
  input  CARREGAR_JUMP,
  input  CLEAR,
  input  CL0CK,
  input  [7:0] SRY,
  input  STR,
  input  RDM,
  output [4:0] ENDERECO_CONTADOR
);

  wire CL0CK_PC_CONTROL, controlled_buffer_1_out, not_1_out;
  wire [4:0] bitselector_1_out;

  assign controlled_buffer_1_out = CL0CK_PC_CONTROL ? CL0CK : 1'bz;  // Controlled_Buffer controlled_buffer_1
  Counter #(.max('h1f), .width(5)) counter_1 (
    .clr(CLEAR), .load(CARREGAR_JUMP), .count(not_1_out), .clk(controlled_buffer_1_out),
    .D(bitselector_1_out), .Q(ENDERECO_CONTADOR));  // open: up, carry
  not not_1 (not_1_out, CARREGAR_JUMP);
  BitSelector #(.group(5)) bitselector_1 (.in(SRY), .out(bitselector_1_out), .sel(1'b0));
  and and_1 (CL0CK_PC_CONTROL, ~STR, ~RDM);  // AND_Gate

  // Notes on the sheet:
  //   CONTADOR DE PROGRAMA
endmodule

module RegistradorDeInstrucao (
  input  [7:0] PALAVRA_MEMORIA,
  input  CL0CK,
  input  CLEAR,
  output [7:0] PALAVRA_REGISTRADA
);

  Register register_1 (.D(PALAVRA_MEMORIA), .clk(CL0CK), .Q(PALAVRA_REGISTRADA), .clr(CLEAR));  // open: en

  // Notes on the sheet:
  //   REGISTRADOR DE INSTRUCAO
endmodule

module UnidadeDeControle (
  input  [7:0] SR0,
  input  [7:0] PALAVRA_REGISTRADA,
  input  [7:0] SR1,
  input  [7:0] SR2,
  input  [7:0] SR3,
  input  [7:0] RA,
  input  [7:0] RAM_DADOS,
  output [7:0] SRY,
  output [7:0] SRX,
  output ENABLE_RA,
  output [7:0] VALOR_REGISTRADOR,
  output [3:0] INSTRUCAO,
  output [1:0] RY,
  output [1:0] RX,
  output EQ,
  output LT,
  output GT,
  output LEQ,
  output GEQ,
  output JMP,
  output MUL,
  output ADD,
  output SUB,
  output MOV,
  output MOVA,
  output RDM,
  output STR,
  output HLT
);

  DecodificadorDeInstrucao decodificadordeinstrucao_1 (
    .INSTRUCAO(INSTRUCAO), .HLT(HLT), .EQ(EQ), .LT(LT), .GT(GT), .LEQ(LEQ), .GEQ(GEQ), .JMP(JMP), .MUL(MUL),
    .ADD(ADD), .SUB(SUB), .MOV(MOV), .MOVA(MOVA), .RDM(RDM), .STR(STR));
  DecodificadorDePalavra decodificadordepalavra_1 (
    .PALAVRA_REGISTRADA(PALAVRA_REGISTRADA), .RY(RY), .RX(RX), .INSTRUCAO(INSTRUCAO));
  Multiplexer #(.disabled("Z"), .select(2), .width(8)) multiplexer_1 (
    .in0(SR0), .in1(SR1), .in2(SR2), .in3(SR3), .out(SRY), .sel(RY));
  or or_1 (ENABLE_RA, EQ, LT, GT, LEQ, GEQ, MUL, ADD, SUB);
  assign VALOR_REGISTRADOR = MOVA ? RA : 8'bz;  // Controlled_Buffer controlled_buffer_1
  assign VALOR_REGISTRADOR = MOV ? SRY : 8'bz;  // Controlled_Buffer controlled_buffer_2
  assign VALOR_REGISTRADOR = RDM ? RAM_DADOS : 8'bz;  // Controlled_Buffer controlled_buffer_3
  Multiplexer #(.disabled("Z"), .select(2), .width(8)) multiplexer_2 (
    .in0(SR0), .in1(SR1), .in2(SR2), .in3(SR3), .out(SRX), .sel(RX));

  // Notes on the sheet:
  //   UNIDADE DE CONTROLE
endmodule

module DecodificadorDePalavra (
  input  [7:0] PALAVRA_REGISTRADA,
  output [1:0] RY,
  output [1:0] RX,
  output [3:0] INSTRUCAO
);


  assign INSTRUCAO = PALAVRA_REGISTRADA[7:4];
  assign RX = PALAVRA_REGISTRADA[3:2];
  assign RY = PALAVRA_REGISTRADA[1:0];

  // Notes on the sheet:
  //   DECODIFICADOR DE PALAVRA
endmodule

module DecodificadorDeInstrucao (
  input  [3:0] INSTRUCAO,
  output EQ,
  output LT,
  output GT,
  output LEQ,
  output GEQ,
  output JMP,
  output MUL,
  output ADD,
  output SUB,
  output MOV,
  output MOVA,
  output RDM,
  output STR,
  output HLT
);

  Comparator #(.width(4)) comparator_1 (.a(INSTRUCAO), .b(4'b0010), .eq(EQ));  // open: gt, lt
  Comparator #(.width(4)) comparator_2 (.a(INSTRUCAO), .b(4'b0011), .eq(LT));  // open: gt, lt
  Comparator #(.width(4)) comparator_3 (.a(INSTRUCAO), .b(4'b0100), .eq(GT));  // open: gt, lt
  Comparator #(.width(4)) comparator_4 (.a(INSTRUCAO), .b(4'b0101), .eq(LEQ));  // open: gt, lt
  Comparator #(.width(4)) comparator_5 (.a(INSTRUCAO), .b(4'b0110), .eq(GEQ));  // open: gt, lt
  Comparator #(.width(4)) comparator_6 (.a(INSTRUCAO), .b(4'b0111), .eq(JMP));  // open: gt, lt
  Comparator #(.width(4)) comparator_7 (.a(INSTRUCAO), .b(4'b1000), .eq(MUL));  // open: gt, lt
  Comparator #(.width(4)) comparator_8 (.a(INSTRUCAO), .b(4'b1001), .eq(ADD));  // open: gt, lt
  Comparator #(.width(4)) comparator_9 (.a(INSTRUCAO), .b(4'b1010), .eq(SUB));  // open: gt, lt
  Comparator #(.width(4)) comparator_10 (.a(INSTRUCAO), .b(4'b1011), .eq(MOV));  // open: gt, lt
  Comparator #(.width(4)) comparator_11 (.a(INSTRUCAO), .b(4'b1100), .eq(MOVA));  // open: gt, lt
  Comparator #(.width(4)) comparator_12 (.a(INSTRUCAO), .b(4'b1101), .eq(RDM));  // open: gt, lt
  Comparator #(.width(4)) comparator_13 (.a(INSTRUCAO), .b(4'b1110), .eq(STR));  // open: gt, lt
  Comparator #(.width(4)) comparator_14 (.a(INSTRUCAO), .b(4'b1111), .eq(HLT));  // open: gt, lt

  // Notes on the sheet:
  //   DECODIFICADOR DE INSTRUCAO
endmodule

module BancoDeRegistradores (
  input  [7:0] VALOR_REGISTRADOR,
  input  CLEAR,
  input  CL0CK,
  input  [1:0] RX,
  input  DMX,
  output [7:0] SR0,
  output [7:0] SR1,
  output [7:0] SR2,
  output [7:0] SR3
);

  wire demultiplexer_1_out0, demultiplexer_1_out1, demultiplexer_1_out2, demultiplexer_1_out3;

  Register register_1 (.D(VALOR_REGISTRADOR), .en(demultiplexer_1_out0), .clk(CL0CK), .Q(SR0), .clr(CLEAR));
  Demultiplexer #(.disabled("Z"), .select(2)) demultiplexer_1 (
    .out0(demultiplexer_1_out0), .out1(demultiplexer_1_out1), .out2(demultiplexer_1_out2),
    .out3(demultiplexer_1_out3), .in(DMX), .sel(RX));
  Register register_2 (.D(VALOR_REGISTRADOR), .en(demultiplexer_1_out1), .clk(CL0CK), .Q(SR1), .clr(CLEAR));
  Register register_3 (.D(VALOR_REGISTRADOR), .en(demultiplexer_1_out2), .clk(CL0CK), .Q(SR2), .clr(CLEAR));
  Register register_4 (.D(VALOR_REGISTRADOR), .en(demultiplexer_1_out3), .clk(CL0CK), .Q(SR3), .clr(CLEAR));

  // Notes on the sheet:
  //   BANCO DE REGISTRADORES
endmodule

module UnidadeLogicaAritmetica (
  input  [7:0] SRX,
  input  [7:0] SRY,
  input  [7:0] RA,
  input  EQ,
  input  LT,
  input  GT,
  input  LEQ,
  input  GEQ,
  input  JMP,
  input  MUL,
  input  ADD,
  input  SUB,
  output [7:0] ULA,
  output VERIFICAR_IGUALDADE_RA
);

  wire A1, and_1_out, and_2_out, and_3_out, and_4_out, and_5_out, and_6_out, comparator_1_eq,
       comparator_1_gt, comparator_3_eq, comparator_4_lt, comparator_5_gt, comparator_6_eq, comparator_6_lt,
       or_1_out, or_2_out, or_3_out;
  wire [7:0] A2, adder_1_out, bitselector_1_out, multiplier_1_out, subtractor_1_out;

  Comparator comparator_1 (.a(SRX), .b(SRY), .gt(comparator_1_gt), .eq(comparator_1_eq));  // open: lt
  Comparator comparator_2 (.a(RA), .b(8'h1), .eq(VERIFICAR_IGUALDADE_RA));  // open: gt, lt
  Multiplier multiplier_1 (.a(SRX), .b(SRY), .out(multiplier_1_out));  // open: cin, cout
  Adder adder_1 (.a(SRX), .b(SRY), .out(adder_1_out));  // open: cin, cout
  Subtractor subtractor_1 (.a(SRX), .b(SRY), .out(subtractor_1_out));  // open: bin, bout
  Comparator comparator_3 (.a(SRX), .b(SRY), .eq(comparator_3_eq));  // open: gt, lt
  Comparator comparator_4 (.a(SRX), .b(SRY), .lt(comparator_4_lt));  // open: gt, eq
  Comparator comparator_5 (.a(SRX), .b(SRY), .gt(comparator_5_gt));  // open: eq, lt
  Comparator comparator_6 (.a(SRX), .b(SRY), .eq(comparator_6_eq), .lt(comparator_6_lt));  // open: gt
  assign A2 = MUL ? multiplier_1_out : 8'bz;  // Controlled_Buffer controlled_buffer_1
  assign A2 = ADD ? adder_1_out : 8'bz;  // Controlled_Buffer controlled_buffer_2
  assign A2 = SUB ? subtractor_1_out : 8'bz;  // Controlled_Buffer controlled_buffer_3
  and and_1 (and_1_out, comparator_3_eq, 1'b1);
  assign A1 = EQ ? and_1_out : 1'bz;  // Controlled_Buffer controlled_buffer_4
  and and_2 (and_2_out, comparator_4_lt, 1'b1);
  assign A1 = LT ? and_2_out : 1'bz;  // Controlled_Buffer controlled_buffer_5
  and and_3 (and_3_out, comparator_5_gt, 1'b1);
  assign A1 = GT ? and_3_out : 1'bz;  // Controlled_Buffer controlled_buffer_6
  or or_1 (or_1_out, comparator_6_eq, comparator_6_lt);
  or or_2 (or_2_out, comparator_1_gt, comparator_1_eq);
  and and_4 (and_4_out, VERIFICAR_IGUALDADE_RA, 1'b1);
  and and_5 (and_5_out, or_1_out, 1'b1);
  and and_6 (and_6_out, or_2_out, 1'b1);
  assign A1 = JMP ? and_4_out : 1'bz;  // Controlled_Buffer controlled_buffer_7
  assign A1 = LEQ ? and_5_out : 1'bz;  // Controlled_Buffer controlled_buffer_8
  assign A1 = GEQ ? and_6_out : 1'bz;  // Controlled_Buffer controlled_buffer_9
  BitSelector #(.group(8), .width(1)) bitselector_1 (.in(A1), .out(bitselector_1_out), .sel(1'b0));
  or or_3 (or_3_out, SUB, MUL, ADD);
  Multiplexer #(.disabled("Z"), .width(8)) multiplexer_1 (.in0(bitselector_1_out), .in1(A2), .out(ULA), .sel(or_3_out));

  // Notes on the sheet:
  //   UNIDADE LOGICA ARITMETICA
endmodule

module RegistradorAcumulador (
  input  [7:0] ULA,
  input  ENABLE_RA,
  input  CL0CK,
  input  CLEAR,
  output [7:0] RA
);

  Register register_1 (.D(ULA), .en(ENABLE_RA), .clk(CL0CK), .Q(RA), .clr(CLEAR));

  // Notes on the sheet:
  //   REGISTRADOR ACUMULADOR
endmodule
